# Fritzing sketch schedule (saved by Fritzing 1.0.1rc)
breadboards: 1

parts:
  Part1 = Arduino Uno (Rev3)  # not connected
  R1 = Resistor [tolerance=±5% power=0.25 resistance=220 package=THT]
  R2 = Resistor [tolerance=±5% power=0.25 resistance=220 package=THT]  # not connected
  S1 = Pushbutton [package=THT]

nets:
  N1: R1.Pin_0, S1.leg0
